// Logisim project tme1-2.circ as structural Verilog
module main (
  input  in_1,
  input  a0,
  input  b0,
  input  a1,
  input  b1,
  input  a2,
  input  b2,
  input  a3,
  input  b3,
  output out_10,
  output out_11,
  output out_12,
  output out_13,
  output out_14
);

  add_4bit add_4bit_1 (
    .a0(a0), .b0(b0), .a1(a1), .b1(b1), .a2(a2), .b2(b2), .a3(a3), .b3(b3), .cin(in_1), .cout(out_14),
    .S0(out_10), .S1(out_11), .S2(out_12), .S3(out_13));
endmodule

module mon_xor (
  input  in_1,
  input  in_2,
  input  in_3
);

  wire and_1_out, and_2_out, not_1_out, not_2_out;

  not not_1 (not_1_out, in_2);
  not not_2 (not_2_out, in_3);
  and and_1 (and_1_out, not_1_out, in_3);
  and and_2 (and_2_out, in_2, not_2_out);
  or or_1 (in_1, and_1_out, and_2_out);
endmodule

module a_and_not_b (
  input  in_1,
  input  in_2,
  input  in_3
);

  wire and_1_out, not_1_out;

  and and_1 (and_1_out, in_1, not_1_out);
  not not_1 (not_1_out, in_3);
endmodule

module mux2 (
  input  in_1,
  input  in_2,
  input  in_3,
  output out_4
);

  wire and_1_out, and_2_out, not_1_out;

  not not_1 (not_1_out, in_1);
  and and_1 (and_1_out, in_1, in_3);
  or or_1 (out_4, and_1_out, and_2_out);
  and and_2 (and_2_out, not_1_out, in_2);
endmodule

module mux_4bits (
  input  in_1,
  input  in_2,
  input  in_3,
  input  in_4,
  input  in_5,
  input  in_6,
  input  in_7,
  input  in_8,
  input  in_9,
  output out_10,
  output out_11,
  output out_12,
  output out_13
);

  mux2 mux2_1 (.in_2(in_3), .in_3(in_7), .in_1(in_1), .out_4(out_11));
  mux2 mux2_2 (.in_2(in_4), .in_3(in_8), .in_1(in_1), .out_4(out_12));
  mux2 mux2_3 (.in_2(in_5), .in_3(in_9), .in_1(in_1), .out_4(out_13));
  mux2 mux2_4 (.in_2(in_2), .in_3(in_6), .in_1(in_1), .out_4(out_10));
endmodule

module mux4 (
  input  i0,
  input  i1,
  input  in_3,
  input  in_4,
  input  in_5,
  input  in_6
);

  wire and_1_out, and_2_out, not_1_out;

  not not_1 (not_1_out, i0);
  and and_1 (and_1_out, not_1_out, in_3);
  // OR_Gate or_1 has open pins: in0=and_1_out, in1=and_2_out, out=open
  and and_2 (and_2_out, i0, in_3);
  // NOT_Gate not_2 has open pins: in=i1, out=open
endmodule

module add_1bit (
  input  cin,
  input  a,
  input  b,
  output S,
  output cout
);

  wire and_1_out, and_2_out, xor_1_out, xor_2_out;

  xor xor_1 (xor_1_out, cin, b);
  xor xor_2 (xor_2_out, a, b);
  and and_1 (and_1_out, cin, xor_2_out);
  xor xor_3 (S, a, xor_1_out);
  and and_2 (and_2_out, a, b);
  or or_1 (cout, and_2_out, and_1_out);
endmodule

module add_4bit (
  input  cin,
  input  a0,
  input  b0,
  input  a1,
  input  b1,
  input  a2,
  input  b2,
  input  a3,
  input  b3,
  output S0,
  output S1,
  output S2,
  output S3,
  output cout
);

  wire and_1_out, and_2_out, and_3_out, and_4_out, and_5_out, and_6_out, and_7_out, and_8_out, or_1_out,
       or_2_out, or_3_out, xor_1_out, xor_2_out, xor_3_out, xor_4_out, xor_5_out, xor_6_out, xor_7_out,
       xor_8_out;

  xor xor_1 (xor_1_out, cin, b0);
  xor xor_2 (xor_2_out, a0, b0);
  xor xor_3 (xor_3_out, or_1_out, b1);
  xor xor_4 (xor_4_out, a1, b1);
  xor xor_5 (xor_5_out, or_2_out, b2);
  xor xor_6 (xor_6_out, a2, b2);
  xor xor_7 (xor_7_out, or_3_out, b3);
  xor xor_8 (xor_8_out, a3, b3);
  and and_1 (and_1_out, cin, xor_2_out);
  and and_2 (and_2_out, or_1_out, xor_4_out);
  and and_3 (and_3_out, or_2_out, xor_6_out);
  xor xor_9 (S0, a0, xor_1_out);
  and and_4 (and_4_out, a0, b0);
  xor xor_10 (S1, a1, xor_3_out);
  and and_5 (and_5_out, a1, b1);
  xor xor_11 (S2, a2, xor_5_out);
  and and_6 (and_6_out, a2, b2);
  and and_7 (and_7_out, or_3_out, xor_8_out);
  or or_1 (or_1_out, and_4_out, and_1_out);
  or or_2 (or_2_out, and_5_out, and_2_out);
  xor xor_12 (S3, a3, xor_7_out);
  and and_8 (and_8_out, a3, b3);
  or or_3 (or_3_out, and_6_out, and_3_out);
  or or_4 (cout, and_8_out, and_7_out);
endmodule

module ALU_v1 (
  input  aluop,
  input  a0,
  input  b0,
  input  a1,
  input  b1,
  input  a2,
  input  b2,
  input  a3,
  input  b3,
  output S0,
  output S1,
  output S2,
  output S3,
  output cout
);

  wire and_1_out, and_2_out, and_3_out, and_4_out, and_5_out, and_6_out, and_7_out, and_8_out,
       multiplexer_1_out, mux2_1_out_4, mux2_2_out_4, mux2_3_out_4, not_1_out, not_2_out, not_3_out,
       not_4_out, or_1_out, or_2_out, or_3_out, xor_1_out, xor_2_out, xor_3_out, xor_4_out, xor_5_out,
       xor_6_out, xor_7_out, xor_8_out;

  not not_1 (not_1_out, b0);
  not not_2 (not_2_out, b1);
  not not_3 (not_3_out, b2);
  not not_4 (not_4_out, b3);
  Multiplexer #(.enable("false")) multiplexer_1 (.in0(b0), .in1(not_1_out), .out(multiplexer_1_out), .sel(aluop));
  mux2 mux2_1 (.in_2(b1), .in_3(not_2_out), .in_1(aluop), .out_4(mux2_1_out_4));
  mux2 mux2_2 (.in_2(b2), .in_3(not_3_out), .in_1(aluop), .out_4(mux2_2_out_4));
  mux2 mux2_3 (.in_2(b3), .in_3(not_4_out), .in_1(aluop), .out_4(mux2_3_out_4));
  xor xor_1 (xor_1_out, aluop, multiplexer_1_out);
  xor xor_2 (xor_2_out, or_1_out, mux2_1_out_4);
  xor xor_3 (xor_3_out, or_2_out, mux2_2_out_4);
  xor xor_4 (xor_4_out, or_3_out, mux2_3_out_4);
  xor xor_5 (xor_5_out, a0, multiplexer_1_out);
  xor xor_6 (xor_6_out, a1, mux2_1_out_4);
  xor xor_7 (xor_7_out, a2, mux2_2_out_4);
  xor xor_8 (xor_8_out, a3, mux2_3_out_4);
  and and_1 (and_1_out, aluop, xor_5_out);
  and and_2 (and_2_out, or_1_out, xor_6_out);
  and and_3 (and_3_out, or_2_out, xor_7_out);
  and and_4 (and_4_out, or_3_out, xor_8_out);
  xor xor_9 (S0, a0, xor_1_out);
  and and_5 (and_5_out, a0, multiplexer_1_out);
  xor xor_10 (S1, a1, xor_2_out);
  and and_6 (and_6_out, a1, mux2_1_out_4);
  xor xor_11 (S2, a2, xor_3_out);
  and and_7 (and_7_out, a2, mux2_2_out_4);
  xor xor_12 (S3, a3, xor_4_out);
  and and_8 (and_8_out, a3, mux2_3_out_4);
  or or_1 (or_1_out, and_5_out, and_1_out);
  or or_2 (or_2_out, and_6_out, and_2_out);
  or or_3 (or_3_out, and_7_out, and_3_out);
  or or_4 (cout, and_8_out, and_4_out);
endmodule

module ALU_v2 (
  input  aluop,
  input  a0,
  input  b0,
  input  a1,
  input  b1,
  input  a2,
  input  b2,
  input  a3,
  input  b3,
  output S0,
  output S1,
  output S2,
  output Zf,
  output CF,
  output S3,
  output cout,
  output Sf
);

  wire and_1_out, and_2_out, and_3_out, and_4_out, and_5_out, and_6_out, and_7_out, and_8_out,
       multiplexer_1_out, mux2_1_out_4, mux2_2_out_4, mux2_3_out_4, not_1_out, not_2_out, not_3_out,
       not_4_out, or_1_out, or_2_out, or_3_out, xor_1_out, xor_2_out, xor_3_out, xor_4_out, xor_5_out,
       xor_6_out, xor_7_out, xor_8_out;

  not not_1 (not_1_out, b0);
  not not_2 (not_2_out, b1);
  not not_3 (not_3_out, b2);
  not not_4 (not_4_out, b3);
  Multiplexer #(.enable("false")) multiplexer_1 (.in0(b0), .in1(not_1_out), .out(multiplexer_1_out), .sel(aluop));
  mux2 mux2_1 (.in_2(b1), .in_3(not_2_out), .in_1(aluop), .out_4(mux2_1_out_4));
  mux2 mux2_2 (.in_2(b2), .in_3(not_3_out), .in_1(aluop), .out_4(mux2_2_out_4));
  mux2 mux2_3 (.in_2(b3), .in_3(not_4_out), .in_1(aluop), .out_4(mux2_3_out_4));
  xor xor_1 (xor_1_out, aluop, multiplexer_1_out);
  xor xor_2 (xor_2_out, or_1_out, mux2_1_out_4);
  xor xor_3 (xor_3_out, or_2_out, mux2_2_out_4);
  xor xor_4 (xor_4_out, or_3_out, mux2_3_out_4);
  xor xor_5 (xor_5_out, a0, multiplexer_1_out);
  xor xor_6 (xor_6_out, a1, mux2_1_out_4);
  xor xor_7 (xor_7_out, a2, mux2_2_out_4);
  xor xor_8 (xor_8_out, a3, mux2_3_out_4);
  and and_1 (and_1_out, aluop, xor_5_out);
  and and_2 (and_2_out, or_1_out, xor_6_out);
  and and_3 (and_3_out, or_2_out, xor_7_out);
  and and_4 (and_4_out, or_3_out, xor_8_out);
  xor xor_9 (S0, a0, xor_1_out);
  and and_5 (and_5_out, a0, multiplexer_1_out);
  xor xor_10 (S1, a1, xor_2_out);
  and and_6 (and_6_out, a1, mux2_1_out_4);
  xor xor_11 (S2, a2, xor_3_out);
  and and_7 (and_7_out, a2, mux2_2_out_4);
  xor xor_12 (S3, a3, xor_4_out);
  and and_8 (and_8_out, a3, mux2_3_out_4);
  or or_1 (or_1_out, and_5_out, and_1_out);
  or or_2 (or_2_out, and_6_out, and_2_out);
  or or_3 (or_3_out, and_7_out, and_3_out);
  or or_4 (cout, and_8_out, and_4_out);
  xor xor_13 (CF, or_3_out, cout);
  nand nand_1 (Zf, S0, S1, S2, S3);

  assign Sf = cout;
endmodule

module Alu_v2_test (
  input  aluop,
  input  a0,
  input  b0,
  input  a1,
  input  b1,
  input  a2,
  input  b2,
  input  a3,
  input  b3,
  output S0,
  output S1,
  output S2,
  output S3,
  output cout
);

  wire add_1bit_1_cout, and_1_out, and_2_out, and_3_out, and_4_out, and_5_out, and_6_out, mux2_1_out_4,
       mux2_2_out_4, mux2_3_out_4, mux2_4_out_4, not_1_out, not_2_out, not_3_out, not_4_out, or_1_out,
       or_2_out, xor_1_out, xor_2_out, xor_3_out, xor_4_out, xor_5_out, xor_6_out;

  mux2 mux2_1 (.in_2(b0), .in_3(not_1_out), .in_1(aluop), .out_4(mux2_1_out_4));
  not not_1 (not_1_out, b0);
  not not_2 (not_2_out, b1);
  not not_3 (not_3_out, b2);
  not not_4 (not_4_out, b3);
  mux2 mux2_2 (.in_2(b1), .in_3(not_2_out), .in_1(aluop), .out_4(mux2_2_out_4));
  mux2 mux2_3 (.in_2(b2), .in_3(not_3_out), .in_1(aluop), .out_4(mux2_3_out_4));
  mux2 mux2_4 (.in_2(b3), .in_3(not_4_out), .in_1(aluop), .out_4(mux2_4_out_4));
  add_1bit add_1bit_1 (.a(a0), .b(mux2_1_out_4), .cin(aluop), .cout(add_1bit_1_cout), .S(S0));
  xor xor_1 (xor_1_out, add_1bit_1_cout, mux2_2_out_4);
  xor xor_2 (xor_2_out, or_1_out, mux2_3_out_4);
  xor xor_3 (xor_3_out, or_2_out, mux2_4_out_4);
  xor xor_4 (xor_4_out, a1, mux2_2_out_4);
  xor xor_5 (xor_5_out, a2, mux2_3_out_4);
  xor xor_6 (xor_6_out, a3, mux2_4_out_4);
  and and_1 (and_1_out, add_1bit_1_cout, xor_4_out);
  and and_2 (and_2_out, or_1_out, xor_5_out);
  and and_3 (and_3_out, or_2_out, xor_6_out);
  xor xor_7 (S1, a1, xor_1_out);
  and and_4 (and_4_out, a1, mux2_2_out_4);
  xor xor_8 (S2, a2, xor_2_out);
  and and_5 (and_5_out, a2, mux2_3_out_4);
  xor xor_9 (S3, a3, xor_3_out);
  and and_6 (and_6_out, a3, mux2_4_out_4);
  or or_1 (or_1_out, and_4_out, and_1_out);
  or or_2 (or_2_out, and_5_out, and_2_out);
  or or_3 (cout, and_6_out, and_3_out);
endmodule
